# Fritzing sketch MeteoLog (saved by Fritzing 0.9.3b)
circuit board: 8.46667cm x 5.64444cm
breadboards: 1

parts:
  Composant1 = Real Time Clock Module - DS1307 RTC Breakout Board
  Composant2 = Arduino Nano (Rev3.0)
  C1 = Ceramic Capacitor [capacitance=100nF package="100 mil [THT, multilayer]"]
  IC2 = DIP - 6 pins [chip_label=IC package="DIP (Dual Inline) [THT]"]
  RJ-1 = RJ-11 Connector with Breakout Board

nets:
  5V: Composant1.5V, Composant2.5V, IC2.5V
  GND: Composant1.GND, Composant2.GND, C1.1, IC2.GND, RJ-1.GND
  N1: Composant1.SCL, Composant2.A5
  N2: Composant1.SDA, Composant2.A4
  N3: Composant2.D2, C1.0, RJ-1.PRB
  N4: Composant2.D10, IC2.SS
  N5: Composant2.D11/MOSI, IC2.MOSI
  N6: Composant2.D12/MISO, IC2.MISO
  N7: Composant2.D13/SCK, IC2.SCK

notes:
  SD CARD
  RTC Clock
  Rain Gauge

custom parts:
  Real Time Clock Module - DS1307 RTC Breakout Board: This a custom designed module for the DS1307 Real Time Clock. The module comes fully assembled and pre-programmed with the current time (ok, so it's our current time - MST). The included Lithium coin cell battery (CR1225 41mAh) will run the module for a minimum of 9 years (17 years typical) without external 5V power. The DS1307 is accessed via the I2C protocol. We've written a test-bed to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
  DIP - 6 pins: A DIP stand-in part for whatever IC you want. With 6 pins on a 300mil dual inline package (DIP) footprint.
